// Digital circuit ALU_OVERTURE.dig as structural Verilog
module ALU_OVERTURE (
  input  [7:0] INSTRUCTION,
  input  [7:0] IN1,
  input  [7:0] IN2,
  input  [7:0] ADDR,
  input  CLK,
  output [7:0] OUT
);

  wire decoder_1_out_7, not_1_out;
  wire [7:0] add_1_s, and_2_out, blockramdualport_1_d, nand_1_out, nor_1_out, or_1_out, sub_1_s;

  Decoder #(.Selector_Bits(3)) decoder_1 (
    .sel(INSTRUCTION[2:0]), .out_7(decoder_1_out_7));  // open: out_0, out_1, out_2, out_3, out_4, out_5, out_6
  not not_1 (not_1_out, INSTRUCTION[7]);
  BlockRAMDualPort #(.AddrBits(8), .Bits(8)) blockramdualport_1 (
    .A(ADDR), .Din(IN1), .str(decoder_1_out_7), .C(CLK), .D(blockramdualport_1_d));
  // And and_1 has open pins: In_1=INSTRUCTION[6], In_2=not_1_out, out=open
  assign or_1_out = IN1 | IN2;  // Or or_1, 8 bits wide
  assign nand_1_out = ~(IN1 & IN2);  // NAnd nand_1, 8 bits wide
  assign nor_1_out = ~(IN1 | IN2);  // NOr nor_1, 8 bits wide
  assign and_2_out = IN1 & IN2;  // And and_2, 8 bits wide
  Add #(.Bits(8)) add_1 (.a(IN1), .b(IN2), .c_i(1'b0), .s(add_1_s));  // open: c_o
  Sub #(.Bits(8)) sub_1 (.a(IN1), .b(IN2), .c_i(1'b0), .s(sub_1_s));  // open: c_o
  Multiplexer #(.Selector_Bits(3), .Bits(8)) multiplexer_1 (
    .sel(INSTRUCTION[2:0]), .in_0(or_1_out), .in_1(nand_1_out), .in_2(nor_1_out), .in_3(and_2_out),
    .in_4(add_1_s), .in_5(sub_1_s), .in_6(blockramdualport_1_d), .in_7({8{1'b0}}), .out(OUT));

  // Notes on the sheet:
  //   OR
  //   NAND
  //   NOR
  //   AND
  //   ADD
  //   SUB
endmodule
