// Digital circuit CONDITION.dig as structural Verilog
module CONDITION (
  input  [7:0] INSTRUCTION,
  input  [7:0] IN,
  output OUT
);

  wire comparator_1_eq, comparator_1_gt, comparator_1_lt, not_1_out, or_1_out, or_2_out;

  Comparator #(.Bits(8), .Signed("true")) comparator_1 (
    .a(IN), .b({8{1'b0}}), .gt(comparator_1_gt), .eq(comparator_1_eq), .lt(comparator_1_lt));
  or or_1 (or_1_out, comparator_1_lt, comparator_1_eq);
  not not_1 (not_1_out, comparator_1_eq);
  or or_2 (or_2_out, comparator_1_gt, comparator_1_eq);
  Multiplexer #(.Selector_Bits(3)) multiplexer_1 (
    .sel(INSTRUCTION[2:0]), .in_0(1'b0), .in_1(comparator_1_eq), .in_2(comparator_1_lt), .in_3(or_1_out),
    .in_4(1'b1), .in_5(not_1_out), .in_6(or_2_out), .in_7(comparator_1_gt), .out(OUT));

  // Notes on the sheet:
  //   NEVER
  //   ALWAYS
endmodule
