// Digital circuit OVERTURE.dig as structural Verilog
module OVERTURE (
  input  [7:0] IN,
  input  NEXT,
  input  EXE,
  input  CLK,
  output [7:0] OUT
);

  wire and_1_out, and_2_out, and_3_out, and_4_out, condition_1_out, decoder_1_out_0, decoder_1_out_1,
       decoder_1_out_2, decoder_1_out_3, multiplexer_2_out, not_1_out, not_2_out, not_3_out, not_4_out,
       or_1_out, or_2_out, or_3_out, or_4_out, register_1_q, register_2_q, register_4_q, register_5_q,
       register_6_q;
  wire [7:0] alu_overture_1_out, blockramdualport_1_d, counter_1_out, counterpreset_1_out, decoder_2_out_0,
       multiplexer_1_out, multiplexer_3_out, multiplexer_4_out, multiplexer_5_out, multiplexer_6_out,
       multiplexer_7_out, multiplexer_8_out, multiplexer_9_out, register_3_q, register_7_q, register_8_q,
       register_9_q, register_10_q, register_11_q, register_12_q, register_13_q;

  Register register_1 (.D(1'b1), .C(CLK), .en(1'b1), .Q(register_1_q));
  Register register_2 (.D(register_1_q), .C(CLK), .en(1'b1), .Q(register_2_q));
  and and_1 (and_1_out, register_1_q, not_1_out);
  not not_1 (not_1_out, register_2_q);
  and and_2 (and_2_out, 1'b1, and_1_out);
  Register #(.Bits(8)) register_3 (.D(IN), .C(and_3_out), .en(1'b1), .Q(register_3_q));
  or or_1 (or_1_out, register_4_q, and_2_out);
  Multiplexer #(.Bits(8)) multiplexer_1 (
    .sel(register_4_q), .in_0({8{1'b0}}), .in_1(register_3_q), .out(multiplexer_1_out));
  or or_2 (or_2_out, and_2_out, NEXT);
  Register register_4 (.D(1'b1), .C(EXE), .en(1'b1), .Q(register_4_q));
  Register register_5 (.D(or_2_out), .C(CLK), .en(1'b1), .Q(register_5_q));
  not not_2 (not_2_out, register_5_q);
  Register register_6 (.D(register_5_q), .C(CLK), .en(1'b1), .Q(register_6_q));
  and and_3 (and_3_out, not_2_out, register_6_q);
  Multiplexer multiplexer_2 (.sel(or_1_out), .in_0(or_2_out), .in_1(1'b0), .out(multiplexer_2_out));
  Counter #(.Bits(8)) counter_1 (.en(1'b1), .C(and_3_out), .clr(1'b0), .out(counter_1_out));  // open: ovf
  Multiplexer #(.Bits(8)) multiplexer_3 (
    .sel(or_1_out), .in_0(counter_1_out), .in_1(counterpreset_1_out), .out(multiplexer_3_out));
  and and_4 (and_4_out, decoder_1_out_3, condition_1_out);
  // Probe on multiplexer_3_out
  BlockRAMDualPort #(.AddrBits(8), .Bits(8)) blockramdualport_1 (
    .A(multiplexer_3_out), .Din(IN), .str(multiplexer_2_out), .C(CLK), .D(blockramdualport_1_d));
  CounterPreset #(.Bits(8), .isProgramCounter("true")) counterpreset_1 (
    .en(or_1_out), .C(and_3_out), .dir(1'b0), .in(register_7_q), .ld(and_4_out), .clr(1'b0),
    .out(counterpreset_1_out));  // open: ovf
  not not_3 (not_3_out, register_4_q);
  // Probe on multiplexer_4_out
  Multiplexer #(.Bits(8)) multiplexer_4 (
    .sel(not_3_out), .in_0(blockramdualport_1_d), .in_1({8{1'b0}}), .out(multiplexer_4_out));
  Decoder #(.Selector_Bits(2)) decoder_1 (
    .sel(multiplexer_4_out[7:6]), .out_0(decoder_1_out_0), .out_1(decoder_1_out_1), .out_2(decoder_1_out_2),
    .out_3(decoder_1_out_3));
  Decoder #(.Selector_Bits(3)) decoder_2 (
    .sel(multiplexer_4_out[2:0]), .out_0(decoder_2_out_0[0]), .out_1(decoder_2_out_0[1]),
    .out_2(decoder_2_out_0[2]), .out_3(decoder_2_out_0[3]), .out_4(decoder_2_out_0[4]),
    .out_5(decoder_2_out_0[5]), .out_6(decoder_2_out_0[6]), .out_7(decoder_2_out_0[7]));
  not not_4 (not_4_out, decoder_1_out_1);
  Multiplexer #(.Bits(8)) multiplexer_5 (
    .sel(decoder_1_out_2), .in_0({8{1'b0}}), .in_1(decoder_2_out_0), .out(multiplexer_5_out));
  ALU_OVERTURE alu_overture_1 (
    .INSTRUCTION(multiplexer_4_out), .IN1(register_8_q), .IN2(register_9_q), .ADDR(register_13_q),
    .CLK(or_2_out), .OUT(alu_overture_1_out));
  or or_3 (or_3_out, decoder_1_out_0, multiplexer_5_out[0]);
  or or_4 (or_4_out, multiplexer_5_out[3], decoder_1_out_1);
  Multiplexer #(.Bits(8)) multiplexer_6 (
    .sel(not_4_out), .in_0(alu_overture_1_out), .in_1(multiplexer_9_out), .out(multiplexer_6_out));
  Multiplexer #(.Bits(8)) multiplexer_7 (
    .sel(decoder_1_out_0), .in_0(multiplexer_9_out), .in_1({2'b00, multiplexer_4_out[5:0]}),
    .out(multiplexer_7_out));
  Register #(.Bits(8)) register_7 (.D(multiplexer_7_out), .C(CLK), .en(or_3_out), .Q(register_7_q));
  Register #(.Bits(8)) register_8 (.D(multiplexer_9_out), .C(CLK), .en(multiplexer_5_out[1]), .Q(register_8_q));
  Register #(.Bits(8)) register_9 (.D(multiplexer_9_out), .C(CLK), .en(multiplexer_5_out[2]), .Q(register_9_q));
  Register #(.Bits(8)) register_10 (.D(multiplexer_6_out), .C(CLK), .en(or_4_out), .Q(register_10_q));
  Register #(.Bits(8)) register_11 (.D(multiplexer_9_out), .C(CLK), .en(multiplexer_5_out[4]), .Q(register_11_q));
  Register #(.Bits(8)) register_12 (.D(multiplexer_9_out), .C(CLK), .en(multiplexer_5_out[5]), .Q(register_12_q));
  Register #(.Bits(8)) register_13 (.D(multiplexer_9_out), .C(CLK), .en(multiplexer_5_out[7]), .Q(register_13_q));
  CONDITION condition_1 (.INSTRUCTION(multiplexer_4_out), .IN(register_10_q), .OUT(condition_1_out));
  Multiplexer #(.Selector_Bits(3), .Bits(8)) multiplexer_8 (
    .sel(multiplexer_4_out[5:3]), .in_0(register_7_q), .in_1(register_8_q), .in_2(register_9_q),
    .in_3(register_10_q), .in_4(register_11_q), .in_5(register_12_q), .in_6(multiplexer_1_out),
    .in_7(register_13_q), .out(multiplexer_8_out));
  Multiplexer #(.Bits(8)) multiplexer_9 (
    .sel(decoder_1_out_2), .in_0({8{1'b0}}), .in_1(multiplexer_8_out), .out(multiplexer_9_out));
  Multiplexer #(.Bits(8)) multiplexer_10 (
    .sel(multiplexer_5_out[6]), .in_0({8{1'b0}}), .in_1(multiplexer_9_out), .out(OUT));

  // Notes on the sheet:
  //   CLK: Hz: 5
  //   INITIALISER
  //   Fixes problem on my fpga where first NEXT pulse does nothing if set to 1
  //   INSTRUCTION
  //   MAIN BUS
endmodule
