// Digital circuit OVERTURE_TOP.dig as structural Verilog
module OVERTURE_TOP (
  input  [7:0] IN,
  input  NEXT,
  input  EXE,
  input  CLK,
  output [7:0] OUT
);

  wire [5:0] overture_1_out;
  wire [7:0] not_1_out;

  assign not_1_out = ~IN;  // Not not_1, 8 bits wide
  OVERTURE overture_1 (.IN(not_1_out), .NEXT(NEXT), .EXE(EXE), .CLK(CLK), .OUT({OUT[7:6], overture_1_out}));
  assign OUT[5:0] = ~overture_1_out;  // Not not_2, 6 bits wide

  // Notes on the sheet:
  //   CLK: Hz: 5
endmodule
